// Logisim project ProgrammableOfficePlanner.circ as structural Verilog
module main (
);

  wire clock_1_out, comparator_alarma_1_y, CONFIRM_out, COUNT_out, DISPLAY_out, numarator_an_1_bisect,
       number_to_day_convertor_1_a0, number_to_day_convertor_1_a1, number_to_day_convertor_1_b0,
       number_to_day_convertor_1_b1, number_to_day_convertor_1_c0, number_to_day_convertor_1_c1,
       number_to_day_convertor_1_d0, number_to_day_convertor_1_d1, number_to_day_convertor_1_e0,
       number_to_day_convertor_1_e1, number_to_day_convertor_1_f0, number_to_day_convertor_1_f1,
       number_to_day_convertor_1_g0, number_to_day_convertor_1_g1, RESET_out, SET_ALARM_out,
       seven_segment_display_1_a, seven_segment_display_1_b, seven_segment_display_1_c,
       seven_segment_display_1_d, seven_segment_display_1_e, seven_segment_display_1_f,
       seven_segment_display_1_g, seven_segment_display_2_a, seven_segment_display_2_b,
       seven_segment_display_2_c, seven_segment_display_2_d, seven_segment_display_2_e,
       seven_segment_display_2_f, seven_segment_display_2_g, seven_segment_display_3_a,
       seven_segment_display_3_b, seven_segment_display_3_c, seven_segment_display_3_d,
       seven_segment_display_3_e, seven_segment_display_3_f, seven_segment_display_3_g,
       seven_segment_display_4_a, seven_segment_display_4_b, seven_segment_display_4_c,
       seven_segment_display_4_d, seven_segment_display_4_e, seven_segment_display_4_f,
       seven_segment_display_4_g, seven_segment_display_5_a, seven_segment_display_5_b,
       seven_segment_display_5_c, seven_segment_display_5_d, seven_segment_display_5_e,
       seven_segment_display_5_f, seven_segment_display_5_g, seven_segment_display_6_a,
       seven_segment_display_6_b, seven_segment_display_6_c, seven_segment_display_6_d,
       seven_segment_display_6_e, seven_segment_display_6_f, seven_segment_display_6_g,
       seven_segment_display_7_a, seven_segment_display_7_b, seven_segment_display_7_c,
       seven_segment_display_7_d, seven_segment_display_7_e, seven_segment_display_7_f,
       seven_segment_display_7_g, seven_segment_display_8_a, seven_segment_display_8_b,
       seven_segment_display_8_c, seven_segment_display_8_d, seven_segment_display_8_e,
       seven_segment_display_8_f, seven_segment_display_8_g, seven_segment_display_9_a,
       seven_segment_display_9_b, seven_segment_display_9_c, seven_segment_display_9_d,
       seven_segment_display_9_e, seven_segment_display_9_f, seven_segment_display_9_g,
       seven_segment_display_10_a, seven_segment_display_10_b, seven_segment_display_10_c,
       seven_segment_display_10_d, seven_segment_display_10_e, seven_segment_display_10_f,
       seven_segment_display_10_g, seven_segment_display_11_a, seven_segment_display_11_b,
       seven_segment_display_11_c, seven_segment_display_11_d, seven_segment_display_11_e,
       seven_segment_display_11_f, seven_segment_display_11_g, seven_segment_display_12_a,
       seven_segment_display_12_b, seven_segment_display_12_c, seven_segment_display_12_d,
       seven_segment_display_12_e, seven_segment_display_12_f, seven_segment_display_12_g,
       seven_segment_display_13_a, seven_segment_display_13_b, seven_segment_display_13_c,
       seven_segment_display_13_d, seven_segment_display_13_e, seven_segment_display_13_f,
       seven_segment_display_13_g, seven_segment_display_14_a, seven_segment_display_14_b,
       seven_segment_display_14_c, seven_segment_display_14_d, seven_segment_display_14_e,
       seven_segment_display_14_f, seven_segment_display_14_g, seven_segment_display_15_a,
       seven_segment_display_15_b, seven_segment_display_15_c, seven_segment_display_15_d,
       seven_segment_display_15_e, seven_segment_display_15_f, seven_segment_display_15_g,
       seven_segment_display_16_a, seven_segment_display_16_b, seven_segment_display_16_c,
       seven_segment_display_16_d, seven_segment_display_16_e, seven_segment_display_16_f,
       seven_segment_display_16_g, seven_segment_display_17_a, seven_segment_display_17_b,
       seven_segment_display_17_c, seven_segment_display_17_d, seven_segment_display_17_e,
       seven_segment_display_17_f, seven_segment_display_17_g, seven_segment_display_18_a,
       seven_segment_display_18_b, seven_segment_display_18_c, seven_segment_display_18_d,
       seven_segment_display_18_e, seven_segment_display_18_f, seven_segment_display_18_g,
       seven_segment_display_19_a, seven_segment_display_19_b, seven_segment_display_19_c,
       seven_segment_display_19_d, seven_segment_display_19_e, seven_segment_display_19_f,
       seven_segment_display_19_g, seven_segment_display_20_a, seven_segment_display_20_b,
       seven_segment_display_20_c, seven_segment_display_20_d, seven_segment_display_20_e,
       seven_segment_display_20_f, seven_segment_display_20_g, START_out, unitate_de_control_1_alarm,
       unitate_de_control_1_difuzor, unitate_de_control_1_display, unitate_de_control_1_min,
       unitate_de_control_1_off, unitate_de_control_1_onn, unitate_de_control_1_ora;
  wire [2:0] numarator_zi_1_zi_sapt;
  wire [3:0] binary_to_decimal_converter_1_decimal, binary_to_decimal_converter_1_unit,
       binary_to_decimal_converter_2_decimal, binary_to_decimal_converter_2_unit,
       binary_to_decimal_converter_3_decimal, binary_to_decimal_converter_3_unit,
       binary_to_decimal_converter_4_decimal, binary_to_decimal_converter_4_unit,
       binary_to_decimal_converter_5_decimal, binary_to_decimal_converter_5_unit,
       binary_to_decimal_converter_6_decimal, binary_to_decimal_converter_6_unit,
       binary_to_decimal_converter_7_decimal, binary_to_decimal_converter_7_unit,
       binary_to_decimal_converter_8_decimal, binary_to_decimal_converter_8_unit,
       binary_to_decimal_converter_9_decimal, binary_to_decimal_converter_9_unit, numarator_an_1_m,
       numarator_an_1_s, numarator_luna_1_luna;
  wire [4:0] algoritm_alarma_1_ora, numarator_ora_1_ora, numarator_zi_1_zi, registru_alarma_1_q_ora,
       temp_generator_1_temperature;
  wire [5:0] algoritm_alarma_1_min, numarator_minut_1_minut, numarator_secunda_1_secunda,
       registru_alarma_1_q_min;
  wire [6:0] numarator_an_1_an;

  seven_segment_display seven_segment_display_1 (
    .data(binary_to_decimal_converter_4_decimal), .a(seven_segment_display_1_a),
    .b(seven_segment_display_1_b), .c(seven_segment_display_1_c), .d(seven_segment_display_1_d),
    .e(seven_segment_display_1_e), .f(seven_segment_display_1_f), .g(seven_segment_display_1_g));
  Clock clock_1 (.out(clock_1_out));
  Button START (.out(START_out));
  Button SET_ALARM (.out(SET_ALARM_out));
  Button DISPLAY (.out(DISPLAY_out));
  Button CONFIRM (.out(CONFIRM_out));
  Button RESET (.out(RESET_out));
  Button COUNT (.out(COUNT_out));
  _7_Segment_Display ORA (
    .g(seven_segment_display_1_g), .f(seven_segment_display_1_f), .a(seven_segment_display_1_a),
    .b(seven_segment_display_1_b), .e(seven_segment_display_1_e), .d(seven_segment_display_1_d),
    .c(seven_segment_display_1_c));  // open: dp
  seven_segment_display seven_segment_display_2 (
    .data(numarator_an_1_m), .a(seven_segment_display_2_a), .b(seven_segment_display_2_b),
    .c(seven_segment_display_2_c), .d(seven_segment_display_2_d), .e(seven_segment_display_2_e),
    .f(seven_segment_display_2_f), .g(seven_segment_display_2_g));
  _7_Segment_Display u_7_segment_display_1 (
    .g(seven_segment_display_3_g), .f(seven_segment_display_3_f), .a(seven_segment_display_3_a),
    .b(seven_segment_display_3_b), .e(seven_segment_display_3_e), .d(seven_segment_display_3_d),
    .c(seven_segment_display_3_c));  // open: dp
  seven_segment_display seven_segment_display_3 (
    .data(binary_to_decimal_converter_4_unit), .a(seven_segment_display_3_a), .b(seven_segment_display_3_b),
    .c(seven_segment_display_3_c), .d(seven_segment_display_3_d), .e(seven_segment_display_3_e),
    .f(seven_segment_display_3_f), .g(seven_segment_display_3_g));
  _7_Segment_Display AN (
    .g(seven_segment_display_2_g), .f(seven_segment_display_2_f), .a(seven_segment_display_2_a),
    .b(seven_segment_display_2_b), .e(seven_segment_display_2_e), .d(seven_segment_display_2_d),
    .c(seven_segment_display_2_c));  // open: dp
  _7_Segment_Display u_7_segment_display_2 (
    .g(seven_segment_display_5_g), .f(seven_segment_display_5_f), .a(seven_segment_display_5_a),
    .b(seven_segment_display_5_b), .e(seven_segment_display_5_e), .d(seven_segment_display_5_d),
    .c(seven_segment_display_5_c));  // open: dp
  _7_Segment_Display u_7_segment_display_3 (
    .g(seven_segment_display_6_g), .f(seven_segment_display_6_f), .a(seven_segment_display_6_a),
    .b(seven_segment_display_6_b), .e(seven_segment_display_6_e), .d(seven_segment_display_6_d),
    .c(seven_segment_display_6_c));  // open: dp
  unitate_de_control unitate_de_control_1 (
    .clk(clock_1_out), .start(START_out), .setare(SET_ALARM_out), .afisare(DISPLAY_out),
    .confirm(CONFIRM_out), .reset(RESET_out), .verif(comparator_alarma_1_y), .OFF(unitate_de_control_1_off),
    .ONN(unitate_de_control_1_onn), .DISPLAY(unitate_de_control_1_display),
    .ALARM(unitate_de_control_1_alarm), .ORA(unitate_de_control_1_ora), .MIN(unitate_de_control_1_min),
    .DIFUZOR(unitate_de_control_1_difuzor));
  seven_segment_display seven_segment_display_4 (
    .data(binary_to_decimal_converter_2_decimal), .a(seven_segment_display_4_a),
    .b(seven_segment_display_4_b), .c(seven_segment_display_4_c), .d(seven_segment_display_4_d),
    .e(seven_segment_display_4_e), .f(seven_segment_display_4_f), .g(seven_segment_display_4_g));
  seven_segment_display seven_segment_display_5 (
    .data(numarator_an_1_s), .a(seven_segment_display_5_a), .b(seven_segment_display_5_b),
    .c(seven_segment_display_5_c), .d(seven_segment_display_5_d), .e(seven_segment_display_5_e),
    .f(seven_segment_display_5_f), .g(seven_segment_display_5_g));
  _7_Segment_Display u_7_segment_display_4 (
    .g(seven_segment_display_8_g), .f(seven_segment_display_8_f), .a(seven_segment_display_8_a),
    .b(seven_segment_display_8_b), .e(seven_segment_display_8_e), .d(seven_segment_display_8_d),
    .c(seven_segment_display_8_c));  // open: dp
  LED OFF (.in(unitate_de_control_1_off));
  LED ONN (.in(unitate_de_control_1_onn));
  LED led_1 (.in(unitate_de_control_1_display));
  LED ALARMA (.in(unitate_de_control_1_alarm));
  LED led_2 (.in(unitate_de_control_1_ora));
  LED led_3 (.in(unitate_de_control_1_min));
  LED DIFUZOR (.in(unitate_de_control_1_difuzor));
  _7_Segment_Display u_7_segment_display_5 (
    .g(seven_segment_display_4_g), .f(seven_segment_display_4_f), .a(seven_segment_display_4_a),
    .b(seven_segment_display_4_b), .e(seven_segment_display_4_e), .d(seven_segment_display_4_d),
    .c(seven_segment_display_4_c));  // open: dp
  _7_Segment_Display u_7_segment_display_6 (
    .g(seven_segment_display_7_g), .f(seven_segment_display_7_f), .a(seven_segment_display_7_a),
    .b(seven_segment_display_7_b), .e(seven_segment_display_7_e), .d(seven_segment_display_7_d),
    .c(seven_segment_display_7_c));  // open: dp
  seven_segment_display seven_segment_display_6 (
    .data(binary_to_decimal_converter_9_decimal), .a(seven_segment_display_6_a),
    .b(seven_segment_display_6_b), .c(seven_segment_display_6_c), .d(seven_segment_display_6_d),
    .e(seven_segment_display_6_e), .f(seven_segment_display_6_f), .g(seven_segment_display_6_g));
  seven_segment_display seven_segment_display_7 (
    .data(binary_to_decimal_converter_2_unit), .a(seven_segment_display_7_a), .b(seven_segment_display_7_b),
    .c(seven_segment_display_7_c), .d(seven_segment_display_7_d), .e(seven_segment_display_7_e),
    .f(seven_segment_display_7_f), .g(seven_segment_display_7_g));
  seven_segment_display seven_segment_display_8 (
    .data(binary_to_decimal_converter_9_unit), .a(seven_segment_display_8_a), .b(seven_segment_display_8_b),
    .c(seven_segment_display_8_c), .d(seven_segment_display_8_d), .e(seven_segment_display_8_e),
    .f(seven_segment_display_8_f), .g(seven_segment_display_8_g));
  seven_segment_display seven_segment_display_9 (
    .data(binary_to_decimal_converter_1_decimal), .a(seven_segment_display_9_a),
    .b(seven_segment_display_9_b), .c(seven_segment_display_9_c), .d(seven_segment_display_9_d),
    .e(seven_segment_display_9_e), .f(seven_segment_display_9_f), .g(seven_segment_display_9_g));
  _7_Segment_Display u_7_segment_display_7 (
    .g(seven_segment_display_9_g), .f(seven_segment_display_9_f), .a(seven_segment_display_9_a),
    .b(seven_segment_display_9_b), .e(seven_segment_display_9_e), .d(seven_segment_display_9_d),
    .c(seven_segment_display_9_c));  // open: dp
  _7_Segment_Display u_7_segment_display_8 (
    .g(seven_segment_display_10_g), .f(seven_segment_display_10_f), .a(seven_segment_display_10_a),
    .b(seven_segment_display_10_b), .e(seven_segment_display_10_e), .d(seven_segment_display_10_d),
    .c(seven_segment_display_10_c));  // open: dp
  seven_segment_display seven_segment_display_10 (
    .data(binary_to_decimal_converter_1_unit), .a(seven_segment_display_10_a),
    .b(seven_segment_display_10_b), .c(seven_segment_display_10_c), .d(seven_segment_display_10_d),
    .e(seven_segment_display_10_e), .f(seven_segment_display_10_f), .g(seven_segment_display_10_g));
  seven_segment_display seven_segment_display_11 (
    .data(binary_to_decimal_converter_6_decimal), .a(seven_segment_display_11_a),
    .b(seven_segment_display_11_b), .c(seven_segment_display_11_c), .d(seven_segment_display_11_d),
    .e(seven_segment_display_11_e), .f(seven_segment_display_11_f), .g(seven_segment_display_11_g));
  _7_Segment_Display u_7_segment_display_9 (
    .g(seven_segment_display_12_g), .f(seven_segment_display_12_f), .a(seven_segment_display_12_a),
    .b(seven_segment_display_12_b), .e(seven_segment_display_12_e), .d(seven_segment_display_12_d),
    .c(seven_segment_display_12_c));  // open: dp
  _7_Segment_Display u_7_segment_display_10 (
    .g(seven_segment_display_11_g), .f(seven_segment_display_11_f), .a(seven_segment_display_11_a),
    .b(seven_segment_display_11_b), .e(seven_segment_display_11_e), .d(seven_segment_display_11_d),
    .c(seven_segment_display_11_c));  // open: dp
  seven_segment_display seven_segment_display_12 (
    .data(binary_to_decimal_converter_6_unit), .a(seven_segment_display_12_a),
    .b(seven_segment_display_12_b), .c(seven_segment_display_12_c), .d(seven_segment_display_12_d),
    .e(seven_segment_display_12_e), .f(seven_segment_display_12_f), .g(seven_segment_display_12_g));
  _7_Segment_Display u_7_segment_display_11 (
    .g(seven_segment_display_13_g), .f(seven_segment_display_13_f), .a(seven_segment_display_13_a),
    .b(seven_segment_display_13_b), .e(seven_segment_display_13_e), .d(seven_segment_display_13_d),
    .c(seven_segment_display_13_c));  // open: dp
  seven_segment_display seven_segment_display_13 (
    .data(binary_to_decimal_converter_5_decimal), .a(seven_segment_display_13_a),
    .b(seven_segment_display_13_b), .c(seven_segment_display_13_c), .d(seven_segment_display_13_d),
    .e(seven_segment_display_13_e), .f(seven_segment_display_13_f), .g(seven_segment_display_13_g));
  _7_Segment_Display u_7_segment_display_12 (
    .g(seven_segment_display_15_g), .f(seven_segment_display_15_f), .a(seven_segment_display_15_a),
    .b(seven_segment_display_15_b), .e(seven_segment_display_15_e), .d(seven_segment_display_15_d),
    .c(seven_segment_display_15_c));  // open: dp
  seven_segment_display seven_segment_display_14 (
    .data(binary_to_decimal_converter_8_decimal), .a(seven_segment_display_14_a),
    .b(seven_segment_display_14_b), .c(seven_segment_display_14_c), .d(seven_segment_display_14_d),
    .e(seven_segment_display_14_e), .f(seven_segment_display_14_f), .g(seven_segment_display_14_g));
  _7_Segment_Display u_7_segment_display_13 (
    .g(seven_segment_display_14_g), .f(seven_segment_display_14_f), .a(seven_segment_display_14_a),
    .b(seven_segment_display_14_b), .e(seven_segment_display_14_e), .d(seven_segment_display_14_d),
    .c(seven_segment_display_14_c));  // open: dp
  _7_Segment_Display u_7_segment_display_14 (
    .g(seven_segment_display_16_g), .f(seven_segment_display_16_f), .a(seven_segment_display_16_a),
    .b(seven_segment_display_16_b), .e(seven_segment_display_16_e), .d(seven_segment_display_16_d),
    .c(seven_segment_display_16_c));  // open: dp
  seven_segment_display seven_segment_display_15 (
    .data(binary_to_decimal_converter_5_unit), .a(seven_segment_display_15_a),
    .b(seven_segment_display_15_b), .c(seven_segment_display_15_c), .d(seven_segment_display_15_d),
    .e(seven_segment_display_15_e), .f(seven_segment_display_15_f), .g(seven_segment_display_15_g));
  seven_segment_display seven_segment_display_16 (
    .data(binary_to_decimal_converter_8_unit), .a(seven_segment_display_16_a),
    .b(seven_segment_display_16_b), .c(seven_segment_display_16_c), .d(seven_segment_display_16_d),
    .e(seven_segment_display_16_e), .f(seven_segment_display_16_f), .g(seven_segment_display_16_g));
  numarator_secunda numarator_secunda_1 (
    .clk(clock_1_out), .enable(unitate_de_control_1_display), .secunda(numarator_secunda_1_secunda));
  seven_segment_display seven_segment_display_17 (
    .data(binary_to_decimal_converter_7_decimal), .a(seven_segment_display_17_a),
    .b(seven_segment_display_17_b), .c(seven_segment_display_17_c), .d(seven_segment_display_17_d),
    .e(seven_segment_display_17_e), .f(seven_segment_display_17_f), .g(seven_segment_display_17_g));
  _7_Segment_Display u_7_segment_display_15 (
    .g(number_to_day_convertor_1_g0), .f(number_to_day_convertor_1_f0), .a(number_to_day_convertor_1_a0),
    .b(number_to_day_convertor_1_b0), .e(number_to_day_convertor_1_e0), .d(number_to_day_convertor_1_d0),
    .c(number_to_day_convertor_1_c0));  // open: dp
  _7_Segment_Display u_7_segment_display_16 (
    .g(seven_segment_display_17_g), .f(seven_segment_display_17_f), .a(seven_segment_display_17_a),
    .b(seven_segment_display_17_b), .e(seven_segment_display_17_e), .d(seven_segment_display_17_d),
    .c(seven_segment_display_17_c));  // open: dp
  _7_Segment_Display u_7_segment_display_17 (
    .g(number_to_day_convertor_1_g1), .f(number_to_day_convertor_1_f1), .a(number_to_day_convertor_1_a1),
    .b(number_to_day_convertor_1_b1), .e(number_to_day_convertor_1_e1), .d(number_to_day_convertor_1_d1),
    .c(number_to_day_convertor_1_c1));  // open: dp
  _7_Segment_Display u_7_segment_display_18 (
    .g(seven_segment_display_18_g), .f(seven_segment_display_18_f), .a(seven_segment_display_18_a),
    .b(seven_segment_display_18_b), .e(seven_segment_display_18_e), .d(seven_segment_display_18_d),
    .c(seven_segment_display_18_c));  // open: dp
  seven_segment_display seven_segment_display_18 (
    .data(binary_to_decimal_converter_7_unit), .a(seven_segment_display_18_a),
    .b(seven_segment_display_18_b), .c(seven_segment_display_18_c), .d(seven_segment_display_18_d),
    .e(seven_segment_display_18_e), .f(seven_segment_display_18_f), .g(seven_segment_display_18_g));
  number_to_day_convertor number_to_day_convertor_1 (
    .data(numarator_zi_1_zi_sapt), .a1(number_to_day_convertor_1_a1), .b1(number_to_day_convertor_1_b1),
    .c1(number_to_day_convertor_1_c1), .d1(number_to_day_convertor_1_d1), .e1(number_to_day_convertor_1_e1),
    .f1(number_to_day_convertor_1_f1), .g1(number_to_day_convertor_1_g1), .a0(number_to_day_convertor_1_a0),
    .b0(number_to_day_convertor_1_b0), .c0(number_to_day_convertor_1_c0), .d0(number_to_day_convertor_1_d0),
    .e0(number_to_day_convertor_1_e0), .f0(number_to_day_convertor_1_f0), .g0(number_to_day_convertor_1_g0));
  algoritm_alarma algoritm_alarma_1 (
    .clk(COUNT_out), .enable_ora(unitate_de_control_1_ora), .enable_min(unitate_de_control_1_min),
    .ora(algoritm_alarma_1_ora), .min(algoritm_alarma_1_min));
  numarator_minut numarator_minut_1 (
    .clk(clock_1_out), .enable(unitate_de_control_1_display), .sec(numarator_secunda_1_secunda),
    .minut(numarator_minut_1_minut));
  registru_alarma registru_alarma_1 (
    .ora(algoritm_alarma_1_ora), .min(algoritm_alarma_1_min), .q_ora(registru_alarma_1_q_ora),
    .q_min(registru_alarma_1_q_min));
  seven_segment_display seven_segment_display_19 (
    .data(binary_to_decimal_converter_3_decimal), .a(seven_segment_display_19_a),
    .b(seven_segment_display_19_b), .c(seven_segment_display_19_c), .d(seven_segment_display_19_d),
    .e(seven_segment_display_19_e), .f(seven_segment_display_19_f), .g(seven_segment_display_19_g));
  _7_Segment_Display u_7_segment_display_19 (
    .g(seven_segment_display_19_g), .f(seven_segment_display_19_f), .a(seven_segment_display_19_a),
    .b(seven_segment_display_19_b), .e(seven_segment_display_19_e), .d(seven_segment_display_19_d),
    .c(seven_segment_display_19_c));  // open: dp
  _7_Segment_Display u_7_segment_display_20 (
    .g(seven_segment_display_20_g), .f(seven_segment_display_20_f), .a(seven_segment_display_20_a),
    .b(seven_segment_display_20_b), .e(seven_segment_display_20_e), .d(seven_segment_display_20_d),
    .c(seven_segment_display_20_c));  // open: dp
  seven_segment_display seven_segment_display_20 (
    .data(binary_to_decimal_converter_3_unit), .a(seven_segment_display_20_a),
    .b(seven_segment_display_20_b), .c(seven_segment_display_20_c), .d(seven_segment_display_20_d),
    .e(seven_segment_display_20_e), .f(seven_segment_display_20_f), .g(seven_segment_display_20_g));
  comparator_alarma comparator_alarma_1 (
    .ora1(numarator_ora_1_ora), .ora2(registru_alarma_1_q_ora), .min1(numarator_minut_1_minut),
    .min2(registru_alarma_1_q_min), .y(comparator_alarma_1_y));
  numarator_ora numarator_ora_1 (
    .clk(clock_1_out), .enable(unitate_de_control_1_display), .min(numarator_minut_1_minut),
    .ora(numarator_ora_1_ora));
  Binary_to_decimal_converter binary_to_decimal_converter_1 (
    .Bin_num({2'b00, numarator_secunda_1_secunda}), .Unit(binary_to_decimal_converter_1_unit),
    .Decimal(binary_to_decimal_converter_1_decimal));
  temp_generator temp_generator_1 (
    .enable(unitate_de_control_1_display), .luna(numarator_luna_1_luna), .ora(numarator_ora_1_ora),
    .temperature(temp_generator_1_temperature));
  numarator_zi numarator_zi_1 (
    .clk(clock_1_out), .enable(unitate_de_control_1_display), .ora(numarator_ora_1_ora),
    .min(numarator_minut_1_minut), .bisect(numarator_an_1_bisect), .luna(numarator_luna_1_luna),
    .zi(numarator_zi_1_zi), .zi_sapt(numarator_zi_1_zi_sapt));
  Binary_to_decimal_converter binary_to_decimal_converter_2 (
    .Bin_num({2'b00, numarator_minut_1_minut}), .Unit(binary_to_decimal_converter_2_unit),
    .Decimal(binary_to_decimal_converter_2_decimal));
  Binary_to_decimal_converter binary_to_decimal_converter_3 (
    .Bin_num({3'b000, temp_generator_1_temperature}), .Unit(binary_to_decimal_converter_3_unit),
    .Decimal(binary_to_decimal_converter_3_decimal));
  Binary_to_decimal_converter binary_to_decimal_converter_4 (
    .Bin_num({3'b000, numarator_ora_1_ora}), .Unit(binary_to_decimal_converter_4_unit),
    .Decimal(binary_to_decimal_converter_4_decimal));
  numarator_luna numarator_luna_1 (
    .clk(clock_1_out), .enable(unitate_de_control_1_display), .zi(numarator_zi_1_zi),
    .bisect(numarator_an_1_bisect), .luna(numarator_luna_1_luna));
  Binary_to_decimal_converter binary_to_decimal_converter_5 (
    .Bin_num({3'b000, numarator_zi_1_zi}), .Unit(binary_to_decimal_converter_5_unit),
    .Decimal(binary_to_decimal_converter_5_decimal));
  Binary_to_decimal_converter binary_to_decimal_converter_6 (
    .Bin_num({4'b0000, numarator_luna_1_luna}), .Unit(binary_to_decimal_converter_6_unit),
    .Decimal(binary_to_decimal_converter_6_decimal));
  numarator_an numarator_an_1 (
    .clk(clock_1_out), .enable(unitate_de_control_1_display), .luna(numarator_luna_1_luna),
    .zi(numarator_zi_1_zi), .m(numarator_an_1_m), .s(numarator_an_1_s), .an(numarator_an_1_an),
    .bisect(numarator_an_1_bisect));
  Binary_to_decimal_converter binary_to_decimal_converter_7 (
    .Bin_num({2'b00, algoritm_alarma_1_min}), .Unit(binary_to_decimal_converter_7_unit),
    .Decimal(binary_to_decimal_converter_7_decimal));
  Binary_to_decimal_converter binary_to_decimal_converter_8 (
    .Bin_num({3'b000, algoritm_alarma_1_ora}), .Unit(binary_to_decimal_converter_8_unit),
    .Decimal(binary_to_decimal_converter_8_decimal));
  Binary_to_decimal_converter binary_to_decimal_converter_9 (
    .Bin_num({1'b0, numarator_an_1_an}), .Unit(binary_to_decimal_converter_9_unit),
    .Decimal(binary_to_decimal_converter_9_decimal));

  // Notes on the sheet:
  //   Ora
  //   An
  //   Minut
  //   Secunda
  //   Luna
  //   Zi
  //   Ora Alarma
  //   Minut Alarma
  //   Ziua saptamanii
  //   Temperatura
endmodule

// VHDL entity temp_generator, as the project stores it:
--------------------------------------------------------------------------------
-- Project :
-- File    :
-- Autor   :
-- Date    :
--
--------------------------------------------------------------------------------
-- Description :
--
--------------------------------------------------------------------------------
library ieee;
use ieee.std_logic_1164.all;
use ieee.numeric_std.all;

entity temp_generator is
  Port (
    enable: in std_logic;
    luna: in std_logic_vector(3 downto 0);
    ora: in std_logic_vector(4 downto 0);
    temperature: out std_logic_vector(4 downto 0)
  );
end temp_generator;

architecture behavioral of temp_generator is

  function random_number(min: natural; max: natural) return std_logic_vector is
  variable range1: natural := max - min + 1;
  variable random_num: natural;
begin

  random_num := (min + natural(random_num) mod range1);
  return std_logic_vector(to_unsigned(random_num, 5));
end function;



begin
  generate_temperature:
    process(enable, luna, ora)
    variable random_num: std_logic_vector(4 downto 0);
  begin
    if enable = '1' then
      if luna = "0001" or luna = "0010" or luna = "1100" then -- iarna
        if ora >= "01000" and ora <= "01111" then -- intervalul 8-12
          random_num := random_number(2, 7);
        elsif ora >= "1101" and ora <= "10100" then -- intervalul 13-20
          random_num := random_number(6, 9);
        else
          random_num := random_number(0, 5);
        end if;
      elsif luna = "0011" or luna = "0100" or luna = "0101" then -- primavara
        if ora >= "01000" and ora <= "01111" then -- intervalul 8-12
          random_num := random_number(8, 14);
        elsif ora >= "1101" and ora <= "10100" then -- intervalul 13-20
          random_num := random_number(13, 20);
        else
          random_num := random_number(6, 10);
        end if;
      elsif luna = "0110" or luna = "0111" or luna = "1000" then -- vara
        if ora >= "01000" and ora <= "01111" then -- intervalul 8-12
          random_num := random_number(15, 20);
        elsif ora >= "1101" and ora <= "10100" then -- intervalul 13-20
          random_num := random_number(21, 30);
        else
          random_num := random_number(10, 17);
        end if;
      elsif luna = "1001" or luna = "1010" or luna = "1011" then -- toamna
        if ora >= "01000" and ora <= "01111" then -- intervalul 8-12
          random_num := random_number(6, 12);
        elsif ora >= "1101" and ora <= "10100" then -- intervalul 13-20
          random_num := random_number(10, 18);
        else
          random_num := random_number(4, 8);
        end if;
      else
        random_num := random_number(0, 31);
      end if;
      
      temperature <= random_num;
    end if;
  end process generate_temperature;
end behavioral;

// VHDL entity number_to_day_convertor, as the project stores it:
--------------------------------------------------------------------------------
-- Project :
-- File    :
-- Autor   :
-- Date    :
--
--------------------------------------------------------------------------------
-- Description :
--
--------------------------------------------------------------------------------

LIBRARY ieee;
USE ieee.std_logic_1164.all;

ENTITY number_to_day_convertor IS

port(data: in std_logic_vector(2 downto 0);
	a1,b1,c1,d1,e1,f1,g1: out std_logic;
	a0,b0,c0,d0,e0,f0,g0: out std_logic
	
	);
  
END number_to_day_convertor;


architecture comportamentala of number_to_day_convertor is
begin

process(data)
begin

	case data is

	when "001" => --Luni
		a0<='0';b0<='0';c0<='0';d0<='1';e0<='1';f0<='1';g0<='0';
		a1<='0';b1<='1';c1<='1';d1<='1';e1<='1';f1<='1';g1<='0';

	when "010" => --Marti
		a0<='0';b0<='1';c0<='1';d0<='0';e0<='1';f0<='1';g0<='1';
		a1<='1';b1<='1';c1<='1';d1<='0';e1<='1';f1<='1';g1<='1';

	when "011" => --Miercuri
		a0<='0';b0<='1';c0<='1';d0<='0';e0<='1';f0<='1';g0<='1';
		a1<='0';b1<='1';c1<='1';d1<='0';e1<='0';f1<='0';g1<='0';

	when "100" => --Joi
		a0<='0';b0<='1';c0<='1';d0<='1';e0<='0';f0<='0';g0<='0';
		a1<='1';b1<='1';c1<='1';d1<='1';e1<='1';f1<='1';g1<='0';

	when "101" => --Vineri
		a0<='0';b0<='1';c0<='1';d0<='1';e0<='1';f0<='1';g0<='1';
		a1<='0';b1<='1';c1<='1';d1<='0';e1<='0';f1<='0';g1<='0';

	when "110" => --Sambata
		a0<='1';b0<='0';c0<='1';d0<='1';e0<='0';f0<='1';g0<='1';
		a1<='1';b1<='1';c1<='1';d1<='0';e1<='1';f1<='1';g1<='1';

	when others => --Duminica
		a0<='1';b0<='1';c0<='1';d0<='1';e0<='1';f0<='1';g0<='0';
		a1<='0';b1<='1';c1<='1';d1<='1';e1<='1';f1<='1';g1<='0';

	end case;

end process;

end architecture;

// VHDL entity Binary_to_decimal_converter, as the project stores it:
--------------------------------------------------------------------------------
-- Project :
-- File    :
-- Autor   :
-- Date    :
--
--------------------------------------------------------------------------------
-- Description :
--
--------------------------------------------------------------------------------
LIBRARY ieee;
USE ieee.std_logic_1164.all;
USE ieee.std_logic_unsigned.all;
USE ieee.std_logic_arith.all;

ENTITY Binary_to_decimal_converter IS
  PORT (
 Bin_num: in std_logic_vector(7 downto 0);
  		Unit: out std_logic_vector(3 downto 0);
  		Decimal: out std_logic_vector(3 downto 0)  
    );
END Binary_to_decimal_converter;

--------------------------------------------------------------------------------
--Complete your VHDL description below
--------------------------------------------------------------------------------

ARCHITECTURE comport OF Binary_to_decimal_converter IS

signal num_int: integer:=0;
signal u,z: integer:=0;
BEGIN

	num_int<=conv_integer(bin_num);
	z<=num_int / 10;
	u<=num_int rem 10;
	process(u)
	begin
		case u is
		when 0 => unit <= x"0";
		when 1 => unit <= x"1";
		when 2 => unit <= x"2";
		when 3 => unit <= x"3";
		when 4 => unit <= x"4";
		when 5 => unit <= x"5";
		when 6 => unit <= x"6";
		when 7 => unit <= x"7";
		when 8 => unit <= x"8";
		when 9 => unit <= x"9";
		when others => unit <=x"f";
		end case;
	end process;
	process(z)
	begin
		case z is
		when 0 => Decimal <= x"0";
		when 1 => Decimal <= x"1";
		when 2 => Decimal <= x"2";
		when 3 => Decimal <= x"3";
		when 4 => Decimal <= x"4";
		when 5 => Decimal <= x"5";
		when 6 => Decimal <= x"6";
		when 7 => Decimal <= x"7";
		when 8 => Decimal <= x"8";
		when 9 => Decimal <= x"9";
		when others => Decimal <=x"f";
		end case;
	end process;
		 

	
END comport;

// VHDL entity seven_segment_display, as the project stores it:
--------------------------------------------------------------------------------
-- Project :
-- File    :
-- Autor   :
-- Date    :
--
--------------------------------------------------------------------------------
-- Description :
--
--------------------------------------------------------------------------------

LIBRARY ieee;
USE ieee.std_logic_1164.all;

ENTITY seven_segment_display IS

port(data: in std_logic_vector(3 downto 0);
	a,b,c,d,e,f,g: out std_logic
	);

end seven_segment_display;


architecture arh of seven_segment_display is
begin

process(data)
begin

	case data is 
		when "0000" => a<='1';b<='1';c<='1';d<='1';e<='1';f<='1';g<='0'; --0
		when "0001" => a<='0';b<='1';c<='1';d<='0';e<='0';f<='0';g<='0'; --1
		when "0010" => a<='1';b<='1';c<='0';d<='1';e<='1';f<='0';g<='1'; --2
		when "0011" => a<='1';b<='1';c<='1';d<='1';e<='0';f<='0';g<='1'; --3
		when "0100" => a<='0';b<='1';c<='1';d<='0';e<='0';f<='1';g<='1'; --4
		when "0101" => a<='1';b<='0';c<='1';d<='1';e<='0';f<='1';g<='1'; --5
		when "0110" => a<='1';b<='0';c<='1';d<='1';e<='1';f<='1';g<='1'; --6
		when "0111" => a<='1';b<='1';c<='1';d<='0';e<='0';f<='0';g<='0'; --7
		when "1000" => a<='1';b<='1';c<='1';d<='1';e<='1';f<='1';g<='1'; --8
		when "1001" => a<='1';b<='1';c<='1';d<='1';e<='0';f<='1';g<='1'; --9
		when others => a<='X';b<='X';c<='X';d<='X';e<='X';f<='X';g<='X'; 
	end case;

end process;

end architecture;

// VHDL entity numarator_an, as the project stores it:
--------------------------------------------------------------------------------
-- Project :
-- File    :
-- Autor   :
-- Date    :
--
--------------------------------------------------------------------------------
-- Description :
--
--------------------------------------------------------------------------------

LIBRARY ieee;
USE ieee.std_logic_1164.all;
use ieee.std_logic_unsigned.all;
use IEEE.NUMERIC_STD.ALL;

ENTITY numarator_an IS
port(
	clk: in std_logic;
	enable: in std_logic;

	luna: in std_logic_vector(3 downto 0);
	zi: in std_logic_vector(4 downto 0);

	m: out std_logic_vector(3 downto 0);
	s: out std_logic_vector(3 downto 0);
	an: out std_logic_vector(6 downto 0);
	bisect: out std_logic
	);

end numarator_an;


architecture ARH of numarator_an is
signal count_an: unsigned(6 downto 0) :="0010111";
signal b: std_logic :='0';
begin

process(clk)
begin
	if enable='1' then
		if rising_edge(clk) then
			if count_an=99 then
				count_an<="0010111";
			elsif luna=12 and zi=31 then
				count_an<=count_an+1;
			end if;
			
		end if;

		if count_an=24 or count_an=28 or count_an=32 or count_an=36 or count_an=40 or count_an=44 or count_an=48 or count_an=52 or count_an=56 or count_an=60 or count_an=64 or count_an=68 or count_an=72 or count_an=76 or count_an=80 or count_an=84 or count_an=88 or count_an=92 or count_an=96 then
			b<='1';
		else
			b<='0';
		end if;
	end if;
end process;



m<="0010";
s<="0000";
an<=std_logic_vector(count_an);
bisect<=b;

end architecture;

// VHDL entity numarator_luna, as the project stores it:
--------------------------------------------------------------------------------
-- Project :
-- File    :
-- Autor   :
-- Date    :
--
--------------------------------------------------------------------------------
-- Description :
--
--------------------------------------------------------------------------------
LIBRARY ieee;
USE ieee.std_logic_1164.all;
use ieee.std_logic_unsigned.all;
use IEEE.NUMERIC_STD.ALL;

ENTITY numarator_luna IS
port(
	clk: in std_logic;
	enable: in std_logic;

	zi: in std_logic_vector(4 downto 0);
	bisect: in std_logic;

	luna: out std_logic_vector(3 downto 0)

	);
end numarator_luna;


architecture ARH of numarator_luna is
signal count_luna: unsigned(3 downto 0) :="0001";

begin
process(clk)
    begin
    if enable='1' then
        if rising_edge(clk) then
        	if count_luna=12 and zi=31 then
        		count_luna<="0001";
        	else
        		if count_luna=2 then
        			if bisect='1' then
        				if zi=29 then
        					count_luna<=count_luna+1;
        				end if;
        			else
        				if zi=28 then
        					count_luna<=count_luna+1;
        				end if;
        			end if;
        		elsif count_luna=1 or count_luna=3 or count_luna=5 or count_luna=7 or count_luna=8 or count_luna=10 or count_luna=12 then
					if zi=31 then
						count_luna<=count_luna+1;
					end if;
			elsif count_luna=4 or count_luna=6 or count_luna=9 or count_luna=11 then
					if zi=30 then
						count_luna<=count_luna+1;
					end if;
        		end if;      		
               
		end if;
	end if;
end if;
end process;

luna<=std_logic_vector(count_luna);

end architecture;

// VHDL entity numarator_zi, as the project stores it:
--------------------------------------------------------------------------------
-- Project :
-- File    :
-- Autor   :
-- Date    :
--
--------------------------------------------------------------------------------
-- Description :
--
--------------------------------------------------------------------------------


LIBRARY ieee;
USE ieee.std_logic_1164.all;
use ieee.std_logic_unsigned.all;
use IEEE.NUMERIC_STD.ALL;

ENTITY numarator_zi IS
port(clk: in std_logic;
	enable: in std_logic;

	ora: in std_logic_vector(4 downto 0);
	min: in std_logic_vector(5 downto 0);
	bisect: in std_logic;
	luna: in std_logic_vector(3 downto 0);
	
	zi: out std_logic_vector(4 downto 0);
	zi_sapt: out std_logic_vector(2 downto 0)

	);
end numarator_zi;


architecture ARH of numarator_zi is

signal count_zi: unsigned(4 downto 0) :="00001";
signal count_zi_sapt: unsigned(2 downto 0):="111";


begin
process(clk)
begin

	if enable='1' then
		if rising_edge(clk) then

		
			if luna=2 then
				if bisect='1' then
					if count_zi=29 then
						count_zi<="00001";
						
					elsif count_zi<29 then 
					
						if ora=23 and min= 59 then
							count_zi<=count_zi+1;
							
							if count_zi_sapt=7 then
								count_zi_sapt<="001";
							else
								count_zi_sapt<=count_zi_sapt+1;
							end if;
							
						end if;	
					end if;	
				else
				
					if count_zi=28 then
						count_zi<="00001";
						
						elsif count_zi<28 then 
						if ora=23 and min= 59 then
							count_zi<=count_zi+1;

							if count_zi_sapt=7 then
								count_zi_sapt<="001";
							else
								count_zi_sapt<=count_zi_sapt+1;
							end if;
							
						end if;
					end if;
				end if;

					
			elsif luna=4 or luna=6 or luna=9 or luna=11 then
					if count_zi=30 then
						count_zi<="00001";
						
					elsif count_zi<30 then 
						if ora=23 and min= 59 then
							count_zi<=count_zi+1;

							if count_zi_sapt=7 then
								count_zi_sapt<="001";
							else
								count_zi_sapt<=count_zi_sapt+1;
								
							end if;
						end if;
					end if;
			elsif luna=1 or luna=3 or luna=5 or luna=7 or luna=8 or luna=10 or luna=12 then
					if count_zi=31 then
						count_zi<="00001";
						
					elsif count_zi<31 then 
						if ora=23 and min= 59 then
							count_zi<=count_zi+1;

							if count_zi_sapt=7 then
								count_zi_sapt<="001";
							else
								count_zi_sapt<=count_zi_sapt+1;
							end if;
						end if;
					end if;
			end if;
		end if;
	end if;
end process;

zi<=std_logic_vector(count_zi);
zi_sapt<=std_logic_vector(count_zi_sapt);


end architecture;

// VHDL entity numarator_ora, as the project stores it:
--------------------------------------------------------------------------------
-- Project :
-- File    :
-- Autor   :
-- Date    :
--
--------------------------------------------------------------------------------
-- Description :
--
--------------------------------------------------------------------------------

LIBRARY ieee;
USE ieee.std_logic_1164.all;
use ieee.std_logic_unsigned.all;
use IEEE.NUMERIC_STD.ALL;

ENTITY numarator_ora IS
  PORT (
  	clk: in std_logic;
  	enable: in std_logic;

	min: in std_logic_vector(5 downto 0);

  	ora: out std_logic_vector(4 downto 0)

  	);
END numarator_ora;

--------------------------------------------------------------------------------
--Complete your VHDL description below
--------------------------------------------------------------------------------

ARCHITECTURE TypeArchitecture OF numarator_ora IS
signal count_ora: unsigned(4 downto 0):="01100";
signal y_temp :std_logic :='0';
BEGIN
process(clk)
begin
	if enable='1' then
		if rising_edge(clk) then
			if count_ora=23 then
				count_ora<="00000";
			elsif min=59 then
				count_ora<=count_ora+1;
			end if;
		end if;
	end if;
end process;
ora<=std_logic_vector(count_ora);


END TypeArchitecture;

// VHDL entity numarator_minut, as the project stores it:
--------------------------------------------------------------------------------
-- Project :
-- File    :
-- Autor   :
-- Date    :
--
--------------------------------------------------------------------------------
-- Description :
--
--------------------------------------------------------------------------------
LIBRARY ieee;
USE ieee.std_logic_1164.all;
use ieee.std_logic_unsigned.all;
use IEEE.NUMERIC_STD.ALL;

ENTITY numarator_minut IS
  PORT (
  	clk: in std_logic;
  	enable: in std_logic;

	sec: in std_logic_vector(5 downto 0);

  	minut: out std_logic_vector(5 downto 0)

  	);
END numarator_minut;

--------------------------------------------------------------------------------
--Complete your VHDL description below
--------------------------------------------------------------------------------

ARCHITECTURE TypeArchitecture OF numarator_minut IS

signal count_minut: unsigned(5 downto 0):="000000";

BEGIN
process(clk)
begin
	if enable='1' then
		if rising_edge(clk) then
			if count_minut=59 then
				count_minut<="000000";
			elsif sec=59 then
				count_minut<=count_minut+1;
			end if;
		end if;
	end if;
end process;

minut<=std_logic_vector(count_minut);


END TypeArchitecture;

// VHDL entity registru_alarma, as the project stores it:
--------------------------------------------------------------------------------
-- Project :
-- File    :
-- Autor   :
-- Date    :
--
--------------------------------------------------------------------------------
-- Description :
--
--------------------------------------------------------------------------------

LIBRARY ieee;
USE ieee.std_logic_1164.all;

ENTITY registru_alarma IS
  PORT (
ora: in std_logic_vector(4 downto 0);
  	   min: in std_logic_vector(5 downto 0);

  	   q_ora: out std_logic_vector(4 downto 0);
  	   q_min: out std_logic_vector(5 downto 0));
end registru_alarma;


architecture comp of registru_alarma is
begin

process(ora)
begin

q_ora<=ora;

end process;

process(min)
begin

q_min<=min;

end process;


end architecture;

// VHDL entity comparator_alarma, as the project stores it:
--------------------------------------------------------------------------------
-- Project :
-- File    :
-- Autor   :
-- Date    :
--
--------------------------------------------------------------------------------
-- Description :
--
--------------------------------------------------------------------------------

LIBRARY ieee;
USE ieee.std_logic_1164.all;

ENTITY comparator_alarma IS
	port(ora1: in std_logic_vector(4 downto 0);
		ora2: in std_logic_vector(4 downto 0);
		min1: in std_logic_vector(5 downto 0);
		min2: in std_logic_vector(5 downto 0);

		y: out std_logic
		);
end comparator_alarma;


architecture ARH of comparator_alarma is
begin

process(ora1,ora2,min1,min2)
begin

	if ora1=ora2 and min1=min2 and ora1/="00000" and min1/="000000" then
		y<='1';
	else
		y<='0';
	end if;
end process;
end architecture;

// VHDL entity unitate_de_control, as the project stores it:
--------------------------------------------------------------------------------
-- Project :
-- File    :
-- Autor   :
-- Date    :
--
--------------------------------------------------------------------------------
-- Description :
--
--------------------------------------------------------------------------------

LIBRARY ieee;
USE ieee.std_logic_1164.all;
use ieee.std_logic_unsigned.all;

entity unitate_de_control is

port(
	clk: in std_logic;
	start: in std_logic;
	setare: in std_logic;
	afisare: in std_logic;
	confirm: in std_logic;
	reset: in std_logic;
	verif: in std_logic;

	OFF: out std_logic;
	ONN: out std_logic;
	DISPLAY: out std_logic;
	ALARM: out std_logic;
	ORA: out std_logic;
	MIN: out std_logic;
	DIFUZOR: out std_logic
	);
	
end unitate_de_control;


architecture ARH of unitate_de_control is
type STATE is (S_IDLE,S_ON,S_ALARMA,S_AFIS,S_ORA,S_MIN);
signal stare,stare_urm: STATE;

begin

process(clk,reset)
begin
	if reset='1' then
		stare<=S_IDLE;
	elsif rising_edge(clk) then
		stare<=stare_urm;
	end if;

end process;

process(stare,start,setare,afisare,confirm,reset,verif)
begin
	case stare is
		when S_IDLE =>
			if start='1' then
				stare_urm<=S_ON;
			else
				stare_urm<=S_IDLE;
			end if;
		when S_ON =>
			if setare='1' then
				stare_urm<=S_ALARMA;
			elsif afisare='1' then 
				stare_urm<=S_AFIS;
			else
				stare_urm<=S_ON;
			end if;

			
		when S_ALARMA =>
			if confirm='1' then
				stare_urm<=S_ORA;
			else
				stare_urm<=S_ALARMA;
			end if;

			
		when S_ORA =>
			if confirm='1' then
				stare_urm<=S_MIN;
			else
				stare_urm<=S_ORA;
			end if;

			
		when S_MIN =>
			if confirm='1' then
				stare_urm<=S_ON;
			elsif reset='1' then
				stare_urm<=S_IDLE;
			else
				stare_urm<=S_MIN;
			end if;

			
		when S_AFIS =>
			if setare='1' then
				stare_urm<=S_ALARMA;
			else
				stare_urm<=S_AFIS;
			end if;


	end case;
end process;

process(stare,start,setare,afisare,confirm,reset,verif)
begin

	OFF<='0'; ONN<='0'; DISPLAY<='0'; ALARM<='0'; ORA<='0'; MIN<='0'; DIFUZOR<='0';

	if verif='1' then
		DIFUZOR<='1';
	end if;

	case stare is
		when S_IDLE => OFF<='1';
		when S_ON => ONN<='1';
		when S_ALARMA => ALARM<='1';ONN<='1';
		WHEN S_AFIS => DISPLAY<='1';ONN<='1';
		WHEN S_ORA => ORA<='1';ONN<='1';
		WHEN S_MIN => MIN<='1';ONN<='1';
			
	end case;

end process;



end architecture;

// VHDL entity numarator_secunda, as the project stores it:
--------------------------------------------------------------------------------
-- Project :
-- File    :
-- Autor   :
-- Date    :
--
--------------------------------------------------------------------------------
-- Description :
--
--------------------------------------------------------------------------------

LIBRARY ieee;
USE ieee.std_logic_1164.all;
use ieee.std_logic_unsigned.all;
use IEEE.NUMERIC_STD.ALL;

ENTITY numarator_secunda IS
  PORT (
  	clk: in std_logic;
  	enable: in std_logic;
  	secunda: out std_logic_vector(5 downto 0)

  	);
END numarator_secunda;


ARCHITECTURE TypeArchitecture OF numarator_secunda IS

signal count_secunda: unsigned(5 downto 0):="000000";

BEGIN
process(clk)
begin
	if enable='1' then
		if rising_edge(clk) then
				if count_secunda=59 then
					count_secunda<="000000";
				else
					count_secunda<=count_secunda+1;
				end if;
		end if;
	end if;
end process;

secunda<=std_logic_vector(count_secunda);

END TypeArchitecture;

// VHDL entity algoritm_alarma, as the project stores it:
--------------------------------------------------------------------------------
-- Project :
-- File    :
-- Autor   :
-- Date    :
--
--------------------------------------------------------------------------------
-- Description :
--
--------------------------------------------------------------------------------

LIBRARY ieee;
USE ieee.std_logic_1164.all;
use ieee.std_logic_unsigned.all;
use IEEE.NUMERIC_STD.ALL;

ENTITY algoritm_alarma IS
port(
clk: in std_logic;
enable_ora: in std_logic;
enable_min: in std_logic;

ora: out std_logic_vector(4 downto 0);
min: out std_logic_vector(5 downto 0)
);
end algoritm_alarma;


architecture ARH of algoritm_alarma is

signal count_ora: unsigned(4 downto 0):="00000";
signal count_min: unsigned(5 downto 0):="000000";

begin

process(clk)
begin
if enable_ora='1' then
if rising_edge(clk) then
if count_ora = 23 then
count_ora<="00000";
elsif count_ora<23 then
count_ora<=count_ora+1;
end if;
end if;
elsif enable_min='1' then
if rising_edge(clk) then
if count_min=59 then
count_min<="000000";
elsif count_min<59 then
count_min<=count_min+1;
end if;
end if;
end if;

end process;


ora<=std_logic_vector(count_ora);
min<=std_logic_vector(count_min);

end architecture;
